// Logisim project ALUProject_Simple.circ as structural Verilog: 1 circuit, main circuit main
module main (
  input  Op3,
  input  Op2,
  input  Op1,
  input  Op0,
  input  [15:0] InputA,
  output [15:0] Output,
  output [1:0] Error
);

  wire adder_1_cout, bit_extender_1_out, Clk_out, decoder_1_out1, decoder_1_out2, decoder_1_out3,
       decoder_1_out4, decoder_1_out5, decoder_1_out6, decoder_1_out7, decoder_1_out8, decoder_1_out10,
       decoder_1_out12, decoder_1_out13, decoder_1_out14, decoder_1_out15, nor_1_out;
  wire [1:0] decoder_1_out11, OMSelect0_out;
  wire [2:0] LMSel0_out, MMSel0_out;
  wire [3:0] bit_extender_2_out, bit_extender_3_out;
  wire [15:0] adder_1_out, and_2_out, divider_1_out, divider_1_rem, multiplexer_1_out, multiplexer_2_out,
       multiplexer_3_out, multiplexer_4_out, multiplier_1_cout, multiplier_1_out, nand_1_out, nor_2_out,
       not_1_out, or_2_out, shifter_1_out, shifter_2_out, xnor_1_out, xor_1_out, xor_2_out;

  Clock Clk (.out(Clk_out));
  Bit_Extender #(.in_width(16), .out_width(1), .\type ("input")) bit_extender_1 (
    .in(multiplier_1_cout), .out(bit_extender_1_out));  // open: extend
  nor nor_1 (nor_1_out, InputA[0], InputA[1], InputA[2], InputA[3], InputA[4], InputA[5], InputA[6], InputA[7], InputA[8], InputA[9], InputA[10], InputA[11], InputA[12], InputA[13], InputA[14], InputA[15]);
  assign xor_1_out = Output ^ {16{Op1}};  // XOR_Gate xor_1, 16 bits wide
  or or_1 (Error[0], bit_extender_1_out, adder_1_cout);
  and and_1 (Error[1], nor_1_out, Op1, Op2);
  Adder #(.width(16)) adder_1 (.a(InputA), .b(xor_1_out), .out(adder_1_out), .cout(adder_1_cout));  // open: cin
  Multiplier #(.width(16)) multiplier_1 (
    .a(Output), .b(InputA), .out(multiplier_1_out), .cout(multiplier_1_cout));  // open: cin
  Divider #(.width(16)) divider_1 (.a(Output), .b(InputA), .out(divider_1_out), .rem(divider_1_rem));  // open: upper
  assign and_2_out = Output & InputA;  // AND_Gate and_2, 16 bits wide
  assign or_2_out = Output | InputA;  // OR_Gate or_2, 16 bits wide
  assign not_1_out = ~InputA;  // NOT_Gate not_1, 16 bits wide
  or MMSel0 (MMSel0_out[0], decoder_1_out1, decoder_1_out2, decoder_1_out7);
  Decoder #(.select(4), .enable("false")) decoder_1 (
    .out1(decoder_1_out1), .out2(decoder_1_out2), .out3(decoder_1_out3), .out4(decoder_1_out4),
    .out5(decoder_1_out5), .out6(decoder_1_out6), .out7(decoder_1_out7), .out8(decoder_1_out8),
    .out9(decoder_1_out11[1]), .out10(decoder_1_out10), .out11(decoder_1_out11[0]), .out12(decoder_1_out12),
    .out13(decoder_1_out13), .out14(decoder_1_out14), .out15(decoder_1_out15), .sel({Op3, Op2, Op1, Op0}));  // open: out0
  assign xor_2_out = Output ^ InputA;  // XOR_Gate xor_2, 16 bits wide
  assign nand_1_out = ~(Output & InputA);  // NAND_Gate nand_1, 16 bits wide
  assign nor_2_out = ~(Output | InputA);  // NOR_Gate nor_2, 16 bits wide
  assign xnor_1_out = ~(Output ^ InputA);  // XNOR_Gate xnor_1, 16 bits wide
  Multiplexer #(.select(3), .width(16), .enable("false")) multiplexer_1 (
    .in0(Output), .in1(adder_1_out), .in2(adder_1_out), .in3(multiplier_1_out), .in4(divider_1_out),
    .in5(divider_1_rem), .out(multiplexer_1_out), .sel(MMSel0_out));  // open: in6, in7
  or MMSel1 (MMSel0_out[1], decoder_1_out3, decoder_1_out2);
  assign bit_extender_2_out = {{3{1'b0}}, Op3};  // Bit_Extender bit_extender_2
  assign bit_extender_3_out = {{3{1'b0}}, Op3};  // Bit_Extender bit_extender_3
  or LMSel0 (LMSel0_out[0], decoder_1_out5, decoder_1_out12, decoder_1_out15, decoder_1_out10);
  or MMSel2 (MMSel0_out[2], decoder_1_out6, decoder_1_out7);
  Shifter #(.width(16)) shifter_1 (.in(InputA), .\dist (bit_extender_2_out), .out(shifter_1_out));
  Shifter #(.width(16), .shift("lr")) shifter_2 (.in(InputA), .\dist (bit_extender_3_out), .out(shifter_2_out));
  Multiplexer #(.select(3), .width(16), .enable("false")) multiplexer_2 (
    .in0(Output), .in1(and_2_out), .in2(or_2_out), .in3(xor_2_out), .in4(not_1_out), .in5(nand_1_out),
    .in6(nor_2_out), .in7(xnor_1_out), .out(multiplexer_2_out), .sel(LMSel0_out));
  or MMSel1_2 (LMSel0_out[1], decoder_1_out4, decoder_1_out12, decoder_1_out10, decoder_1_out14);
  or MMSel2_2 (LMSel0_out[2], decoder_1_out13, decoder_1_out15, decoder_1_out14, decoder_1_out10);
  Multiplexer #(.select(2), .width(16), .enable("false")) multiplexer_3 (
    .in0(Output), .in1(shifter_1_out), .in2(shifter_2_out), .out(multiplexer_3_out), .sel(decoder_1_out11));  // open: in3
  or OMSelect0 (OMSelect0_out[0], decoder_1_out1, decoder_1_out2, decoder_1_out3, decoder_1_out6, decoder_1_out7, decoder_1_out11[1], decoder_1_out11[0]);
  Multiplexer #(.select(2), .width(16), .enable("false")) multiplexer_4 (
    .in0(Output), .in1(multiplexer_3_out), .in2(multiplexer_2_out), .in3(multiplexer_1_out),
    .out(multiplexer_4_out), .sel(OMSelect0_out));
  or OMSelect1 (OMSelect0_out[1], decoder_1_out1, decoder_1_out2, decoder_1_out3, decoder_1_out6, decoder_1_out7, decoder_1_out4, decoder_1_out5, decoder_1_out10, decoder_1_out12, decoder_1_out13, decoder_1_out14, decoder_1_out15);
  Register #(.width(16)) ACC (.D(multiplexer_4_out), .Q(Output), .clk(Clk_out), .clr(decoder_1_out8));  // open: en

  // Notes on the sheet:
  //   Error Handling
  //   MathMux
  //   LSHIFT
  //   RSHIFT
  //   LogicMux
  //   ShiftMux
  //   OutMux
endmodule
